# Fritzing sketch triggerBoard (saved by Fritzing 0.9.3b)

parts:
  Componente1 = Arduino Uno (Rev3) - ICSP
  U1 = 2-Channel 5v Relay Shield [package=relay-2ch5v10a]
  U3 = 2.5mm Audio Jack [package=stereojack2.5mm_specia_pogopins]
  J1 = Power Jack [package=power_jack_combo]
  J2 = Power Jack [package=power_jack_combo]
  D1 = Diode [package=diode-1n4001]
  D2 = Diode [package=diode-1n4001]

nets:
  N1: Componente1.D8, U1.IN2
  N2: Componente1.D9_PWM, U1.IN1
  N3: Componente1.D12/MISO, U3.SLEEVE
  5V: Componente1.5V, U1.VCC
  GND: Componente1.GND, U1.GND, U3.LEFT
  N4: U1.K1-In, J1.GND
  N5: U1.K1-On, D1.A
  N6: U1.K2-In, J2.GNDBREAK
  N7: U1.K2-Off, U1.K2-On, D2.A
  N8: J1.PWR, D1.C
  N9: J2.PWR, D2.C

notes:
  Camera A
  Camera B
  Foot pedal input

custom parts:
  2-Channel 5v Relay Shield: 2 Channel 5v Relay Shield w. 2x SPD-06VDC-SD-C
